// Digital circuit Prueba2.dig as structural Verilog
module Prueba2 (
  input  HUMEDAD,
  input  AGUA,
  input  BOMBA,
  input  ON,
  input  [2:0] TEMP,
  input  CLK,
  output ANDP,
  output [7:0] SMUX,
  output [7:0] OUTF,
  output OUT
);

  wire and_2_out, and_3_out, CONT_ovf, FFD1_nq, FFD2_q, not_1_out, not_2_out, or_1_out;

  and and_1 (ANDP, HUMEDAD, AGUA, BOMBA, ON);
  Multiplexer #(.Selector_Bits(3), .Bits(8)) multiplexer_1 (
    .sel(TEMP), .in_0(8'h1e), .in_1(8'h28), .in_2(8'h32), .in_3(8'h3c), .in_4(8'h46), .in_5(8'h50),
    .in_6(8'h5a), .in_7(8'h5a), .out(SMUX));
  D_FF FFD1 (.D(ANDP), .C(CLK), .nQ(FFD1_nq));  // open: Q
  and and_2 (and_2_out, ANDP, FFD1_nq);
  CounterPreset #(.Bits(8)) CONT (
    .en(ANDP), .C(CLK), .dir(1'b1), .in(SMUX), .ld(and_2_out), .clr(1'b0), .out(OUTF), .ovf(CONT_ovf));
  and and_3 (and_3_out, ANDP, CONT_ovf);
  not not_1 (not_1_out, ANDP);
  or or_1 (or_1_out, FFD2_q, and_3_out);
  D_FF_AS FFD2 (.Set(1'b0), .D(or_1_out), .C(CLK), .Clr(not_1_out), .Q(FFD2_q));  // open: nQ
  not not_2 (not_2_out, FFD2_q);
  and and_4 (OUT, ANDP, not_2_out);
endmodule
